// Digital circuit Full Adder 4 bits.dig as structural Verilog
module Full_Adder_4_bits (
  input  A3,
  input  A2,
  input  A1,
  input  A0,
  input  B3,
  input  B2,
  input  B1,
  input  B0,
  input  CI,
  output CO,
  output S3,
  output S2,
  output S0,
  output S1
);

  wire full_adder_2_co, full_adder_3_co, full_adder_4_co;

  Full_Adder full_adder_1 (.CI(full_adder_2_co), .A(A3), .B(B3), .S(S3), .CO(CO));
  Full_Adder full_adder_2 (.CI(full_adder_3_co), .A(A2), .B(B2), .S(S2), .CO(full_adder_2_co));
  Full_Adder full_adder_3 (.CI(full_adder_4_co), .A(A1), .B(B1), .S(S1), .CO(full_adder_3_co));
  Full_Adder full_adder_4 (.CI(CI), .A(A0), .B(B0), .S(S0), .CO(full_adder_4_co));

  // Notes on the sheet:
  //   4 BIT FULL ADDER
endmodule
