// Digital circuit Full Adder 8 bits.dig as structural Verilog
module Full_Adder_8_bits (
  input  B3,
  input  B2,
  input  A2,
  input  A3,
  input  B0,
  input  B1,
  input  B1_2,
  input  B0_2,
  input  A1,
  input  A0,
  input  A3_2,
  input  B2_2,
  input  A0_2,
  input  B3_2,
  input  A2_2,
  input  A1_2,
  input  CI,
  output S1,
  output S2,
  output S2_2,
  output S3,
  output S0,
  output S0_2,
  output S3_2,
  output S1_2,
  output CO
);

  wire full_adder_4_bits_1_co;

  Full_Adder_4_bits full_adder_4_bits_1 (
    .A3(A3), .A2(A2), .A1(A1), .A0(A0), .B3(B3), .B2(B2), .B1(B1_2), .B0(B0_2), .CI(CI),
    .CO(full_adder_4_bits_1_co), .S3(S3), .S2(S2), .S0(S0), .S1(S1));
  Full_Adder_4_bits full_adder_4_bits_2 (
    .A3(A3_2), .A2(A2_2), .A1(A1_2), .A0(A0_2), .B3(B3_2), .B2(B2_2), .B1(B1), .B0(B0),
    .CI(full_adder_4_bits_1_co), .CO(CO), .S3(S3_2), .S2(S2_2), .S0(S0_2), .S1(S1_2));

  // Notes on the sheet:
  //   8 BIT FULL ADDER
endmodule
