// Digital circuit Full Adder.dig as structural Verilog
module Full_Adder (
  input  CI,
  input  A,
  input  B,
  output S,
  output CO
);

  wire half_adder_1_c, half_adder_1_s, half_adder_2_c;

  Half_Adder half_adder_1 (.A(A), .B(B), .S(half_adder_1_s), .C(half_adder_1_c));
  Half_Adder half_adder_2 (.A(CI), .B(half_adder_1_s), .S(S), .C(half_adder_2_c));
  or or_1 (CO, half_adder_2_c, half_adder_1_c);

  // Notes on the sheet:
  //   Full Adder
endmodule
