// Digital circuit Half Adder.dig as structural Verilog
module Half_Adder (
  input  A,
  input  B,
  output S,
  output C
);

  xor xor_1 (S, A, B);
  and and_1 (C, B, A);

  // Notes on the sheet:
  //   Half Adder
endmodule
