// Digital circuit Logic Gates.dig as structural Verilog
module Logic_Gates (
  input  F,
  input  F_2,
  input  in_3,
  input  in_4,
  input  in_5,
  input  in_6,
  input  in_7,
  input  in_8,
  input  in_9,
  input  in_10,
  input  in_11,
  input  in_12,
  input  in_13,
  input  in_14,
  input  in_15,
  input  in_16,
  input  in_17,
  input  in_18,
  input  in_19,
  input  in_20
);

  wire and_1_out, fgpfet_1_s, nand_1_out, nfet_1_d, nfet_1_s, nfet_2_s, nfet_3_s, nfet_4_d, nfet_6_s,
       nor_1_out, or_1_out, pfet_1_s, pfet_3_d, pfet_4_s, pfet_5_s, pfet_7_s;

  nor nor_1 (nor_1_out, in_9, in_10);
  LED led_1 (.in(nor_1_out));
  PFET pfet_1 (.G(in_7), .S(pfet_1_s), .D(1'b1));
  nand nand_1 (nand_1_out, in_16, in_15);
  and and_1 (and_1_out, in_3, in_4);
  or or_1 (or_1_out, in_5, in_6);
  NFET nfet_1 (.G(pfet_1_s), .D(nfet_1_d), .S(nfet_1_s));
  LED led_2 (.in(and_1_out));
  LED led_3 (.in(or_1_out));
  PFET pfet_2 (.G(in_8), .S(1'b1), .D(nfet_1_d));
  LED led_4 (.in(nand_1_out));
  LED led_5 (.in(nfet_1_s));
  NFET nfet_2 (.G(F), .D(F_2), .S(nfet_2_s));
  NFET nfet_3 (.G(in_12), .D(1'b1), .S(nfet_3_s));
  PFET pfet_3 (.G(in_20), .S(1'b1), .D(pfet_3_d));
  LED led_6 (.in(nfet_2_s));
  NFET nfet_4 (.G(in_11), .D(nfet_4_d), .S(1'b1));
  NFET nfet_5 (.G(nfet_3_s), .D(1'b1), .S(nfet_4_d));
  PFET pfet_4 (.G(pfet_5_s), .S(pfet_4_s), .D(1'b1));
  PFET pfet_5 (.G(in_14), .S(pfet_5_s), .D(in_13));
  PFET pfet_6 (.G(in_19), .S(pfet_3_d), .D(1'b1));
  LED led_7 (.in(pfet_3_d));
  LED led_8 (.in(nfet_4_d));
  LED led_9 (.in(pfet_4_s));
  PFET pfet_7 (.G(in_17), .S(pfet_7_s), .D(1'b1));
  FGPFET fgpfet_1 (.G(in_18), .S(fgpfet_1_s), .D(1'b1));
  NFET nfet_6 (.G(fgpfet_1_s), .D(pfet_7_s), .S(nfet_6_s));
  LED led_10 (.in(nfet_6_s));

  // Notes on the sheet:
  //   AND GATE
  //   OR GATE
  //   NOR GATE
  //   NAND GATE
endmodule
