// Digital circuit Rom and first circuit.dig as structural Verilog
module Rom_and_first_circuit (
  input  in_1,
  input  in_2,
  input  clk,
  output [2:0] out_3
);

  wire nor_1_out, nor_2_out;
  wire [2:0] add_1_s, register_1_q;

  Add #(.Bits(3)) add_1 (.a(register_1_q), .b(3'b001), .c_i(1'b0), .s(add_1_s));  // open: c_o
  nor nor_1 (nor_1_out, in_1, nor_2_out);
  nor nor_2 (nor_2_out, nor_1_out, in_2);
  Register #(.Bits(3)) register_1 (.D(add_1_s), .C(clk), .en(clk), .Q(register_1_q));
  LED led_1 (.in(nor_1_out));
  LED led_2 (.in(nor_2_out));
  ROM #(.AddrBits(3), .Bits(3)) ColorsRom (.A(register_1_q), .sel(1'b1), .D(out_3));

  // Notes on the sheet:
  //   Reset
  //   Set
  //   Latches / Flip-Flop
  //   Program Counter
  //   contents of ColorsRom (hex, n*v repeats v):
  //   2,6,2,1,7,3,1,4
endmodule
